# Fritzing sketch ChuckArduino (saved by Fritzing 0.9.3b)

parts:
  Composant1 = Arduino Uno (Rev3)
  U1 = POT [package=pot_mammoth]
  LCD2004-I2C1 = LCD2004-I2C

nets:
  N1: Composant1.A1, U1.A
  N2: Composant1.A4/SDA, LCD2004-I2C1.SDA
  N3: Composant1.A5/SCL, LCD2004-I2C1.SCL
  5V: Composant1.5V, LCD2004-I2C1.VCC
  GND: Composant1.GND, LCD2004-I2C1.GND

notes:
  Alimentation carte et potentiometre
  ---------------------------------------------------
  Vers petits connecteurs 2 broches de la carte:
  Rouge = +
  Brun = -
  Alimentation LEDS RGB
  ----------------------------------
  Faisceaux des leds venants de la barre de connecteurs de la carte:
  R = Couleur rouge = Fil Jaune = pins 3/9
  G = Couleur verte = Fil Vert = pins 5/10
  B = Couleur bleue = Fil Bleu = pins 6/11
  Uniquement connecteurs PWM pour modulation de fréquence (symboles ~) pour les rendre dimmable et permettre le mélange des couleurs
  Brochage ecran LCD
  --------------------------------
  GND => vers GND de l'Arduino
  VCC => vers broche 5V de l'Arduino
  SDA => Pin Data vers broche A4 de l'Arduino
  SCL => Pin Clock vers broche A5 de l'Arduino

custom parts:
  LCD2004-I2C: A standard character display with 4x20 characters. Comes in many colors with LCM2004 IIC attached.
